# Fritzing sketch PIR-Prototype (saved by Fritzing 0.9.9b)

parts:
  M1 = Arduino Nano 33 IOT-tht
  PIR1 = PIR sensor

nets:
  N1: M1.pin_2, PIR1.VDD
  N2: M1.pin_14, M1.pin_19, PIR1.GND
  N3: M1.pin_26, PIR1.SIG

custom parts:
  Arduino Nano 33 IOT-tht: The Arduino Nano 33 IoT is the easiest and cheapest point of entry to enhance existing devices (and creating new ones) to be part of the IoT and designing pico-network applications. Whether you are looking at building a sensor network connected to your office or home router, or if you want to create a BLE device sending data to a cellphone, the Nano 33 IoT is your one-stop-solution for many of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
